// Logisim project ceepoo.circ as structural Verilog: 6 circuits, main circuit registre
module bboard (
  input  [7:0] in_1,
  input  [1:0] in_2,
  input  str,
  input  ld,
  input  ena,
  input  set,
  input  _0,
  input  [2:0] regsel,
  input  cnt,
  input  wipe,
  input  _8sa,
  input  _16sa,
  input  tmpset,
  input  [2:0] in_14,
  input  [1:0] in_15
);

  wire not_1_out, or_1_out;
  wire [1:0] demultiplexer_1_out0, demultiplexer_1_out1, demultiplexer_1_out2, demultiplexer_1_out3,
       demultiplexer_1_out4, demultiplexer_1_out5, demultiplexer_1_out6, demultiplexer_1_out7;
  wire [7:0] _8_MAR_q, alu_1_o, register_1_q, registre_1_o, registre_1_out_4, registre_2_out_4,
       registre_3_out_4, registre_4_out_4, registre_5_out_4, registre_6_out_4, registre_7_out_4,
       registre_8_out_4, registre_9_out_4, registre_10_out_4;
  wire [15:0] counter_1_q;

  // Probe on in_1
  registre registre_1 (.I(in_1), .s_e(in_2), .O(registre_1_o), .out_4(registre_1_out_4));  // open: in_2
  // Probe on registre_1_out_4
  Demultiplexer #(.select(3), .width(2)) demultiplexer_1 (
    .out0(demultiplexer_1_out0), .out1(demultiplexer_1_out1), .out2(demultiplexer_1_out2),
    .out3(demultiplexer_1_out3), .out4(demultiplexer_1_out4), .out5(demultiplexer_1_out5),
    .out6(demultiplexer_1_out6), .out7(demultiplexer_1_out7), .in({set, ena}), .sel(regsel));  // open: en
  registre registre_2 (
    .I(registre_1_o), .s_e(demultiplexer_1_out1), .O(registre_1_o), .out_4(registre_2_out_4), .in_2(wipe));
  registre registre_3 (
    .I(registre_1_o), .s_e(demultiplexer_1_out2), .O(registre_1_o), .out_4(registre_3_out_4), .in_2(wipe));
  registre registre_4 (
    .I(registre_1_o), .s_e(demultiplexer_1_out0), .O(registre_1_o), .out_4(registre_4_out_4), .in_2(wipe));
  // Probe on registre_2_out_4
  // Probe on registre_3_out_4
  // Probe on registre_4_out_4
  Clock clock_1 ();  // open: out
  registre registre_5 (
    .I(registre_1_o), .s_e(demultiplexer_1_out4), .O(registre_1_o), .out_4(registre_5_out_4), .in_2(wipe));
  registre registre_6 (
    .I(registre_1_o), .s_e(demultiplexer_1_out3), .O(registre_1_o), .out_4(registre_6_out_4), .in_2(wipe));
  registre registre_7 (
    .I(registre_1_o), .s_e(demultiplexer_1_out5), .O(registre_1_o), .out_4(registre_7_out_4), .in_2(wipe));
  // Probe on registre_7_out_4
  // Probe on registre_5_out_4
  // Probe on registre_6_out_4
  registre registre_8 (
    .I(registre_1_o), .s_e(demultiplexer_1_out6), .O(registre_1_o), .out_4(registre_8_out_4), .in_2(wipe));
  registre registre_9 (
    .I(registre_1_o), .s_e(demultiplexer_1_out7), .O(registre_1_o), .out_4(registre_9_out_4), .in_2(wipe));
  // Probe on registre_8_out_4
  // Probe on registre_9_out_4
  Register _8_MAR (.D(registre_1_o), .Q(_8_MAR_q), .clk(_8sa));  // open: en, clr
  // Probe on registre_1_o
  // Probe on registre_1_o
  // Probe on registre_1_o
  // Probe on registre_1_o
  // Probe on {registre_1_o, _8_MAR_q}
  not not_1 (not_1_out, _16sa);
  or or_1 (or_1_out, cnt, _16sa);
  Register register_1 (.D(registre_1_o), .Q(register_1_q), .clk(tmpset));  // open: en, clr
  ALU alu_1 (.op(in_14), .o(alu_1_o), .a(registre_1_o), .b(register_1_q));  // open: cin, zero, cout, a_larger, eq
  registre registre_10 (.I(alu_1_o), .s_e(in_15), .O(registre_1_o), .out_4(registre_10_out_4));  // open: in_2
  // Probe on registre_10_out_4
  Counter #(.width(16), .max('hffff)) counter_1 (
    .load(_16sa), .D({registre_1_o, _8_MAR_q}), .count(not_1_out), .Q(counter_1_q), .clk(or_1_out), .clr(_0));  // open: carry
  RAM #(.addrWidth(16)) ram_1 (.addr(counter_1_q), .data(registre_1_o), .clk(str), .ld(ld));  // open: sel, clr
endmodule

module registre (
  input  [7:0] I,
  input  in_2,
  input  [1:0] s_e,
  output [7:0] out_4,
  output [7:0] O
);

  Register register_1 (.D(I), .Q(out_4), .clk(s_e[1]), .clr(in_2));  // open: en
  assign O = s_e[0] ? out_4 : 8'bz;  // Controlled_Buffer controlled_buffer_1
  Pull_Resistor pull_resistor_1 (.node(s_e[0]));
endmodule

module ALU (
  input  [7:0] a,
  input  [7:0] b,
  input  cin,
  input  [2:0] op,
  output zero,
  output [7:0] o,
  output cout,
  output a_larger,
  output eq
);

  wire adder_1_cout, decoder_1_out0, decoder_1_out1, decoder_1_out2, decoder_1_out3, decoder_1_out4,
       decoder_1_out5, decoder_1_out6, or_2_out, sh_l_1_cout, sh_r_1_cout;
  wire [7:0] adder_1_out, and_1_out, buffer_1_out, not_1_out, or_1_out, sh_l_1_out_3, sh_r_1_out_4, xor_1_out;

  assign not_1_out = ~a;  // NOT_Gate not_1, 8 bits wide
  Comparator #(.mode("unsigned")) comparator_1 (.a(a), .b(b), .gt(a_larger), .eq(eq));  // open: lt
  assign xor_1_out = a ^ b;  // XOR_Gate xor_1, 8 bits wide
  assign or_1_out = a | b;  // OR_Gate or_1, 8 bits wide
  assign and_1_out = a & b;  // AND_Gate and_1, 8 bits wide
  assign o = decoder_1_out2 ? sh_l_1_out_3 : 8'bz;  // Controlled_Buffer controlled_buffer_1
  sh_l sh_l_1 (.in_2(a), .out_3(sh_l_1_out_3), .cin(cin), .cout(sh_l_1_cout));
  assign cout = decoder_1_out2 ? sh_l_1_cout : 1'bz;  // Controlled_Buffer controlled_buffer_2
  assign cout = decoder_1_out1 ? sh_r_1_cout : 1'bz;  // Controlled_Buffer controlled_buffer_3
  assign o = decoder_1_out1 ? sh_r_1_out_4 : 8'bz;  // Controlled_Buffer controlled_buffer_4
  sh_r sh_r_1 (.in_1(a), .out_4(sh_r_1_out_4), .cout(sh_r_1_cout), .cin(cin));
  Adder adder_1 (.a(a), .b(b), .out(adder_1_out), .cin(cin), .cout(adder_1_cout));
  assign o = decoder_1_out0 ? adder_1_out : 8'bz;  // Controlled_Buffer controlled_buffer_5
  assign cout = decoder_1_out0 ? adder_1_cout : 1'bz;  // Controlled_Buffer controlled_buffer_6
  Decoder #(.select(3)) decoder_1 (
    .out0(decoder_1_out0), .out1(decoder_1_out1), .out2(decoder_1_out2), .out3(decoder_1_out3),
    .out4(decoder_1_out4), .out5(decoder_1_out5), .out6(decoder_1_out6), .sel(op));  // open: out7, en
  assign o = decoder_1_out6 ? xor_1_out : 8'bz;  // Controlled_Buffer controlled_buffer_7
  assign o = decoder_1_out5 ? or_1_out : 8'bz;  // Controlled_Buffer controlled_buffer_8
  assign o = decoder_1_out4 ? and_1_out : 8'bz;  // Controlled_Buffer controlled_buffer_9
  assign o = decoder_1_out3 ? not_1_out : 8'bz;  // Controlled_Buffer controlled_buffer_10
  assign buffer_1_out = o;  // Buffer buffer_1, 8 bits wide
  Pull_Resistor pull_resistor_1 (.node(buffer_1_out));
  or or_2 (or_2_out, buffer_1_out[0], buffer_1_out[1], buffer_1_out[2], buffer_1_out[3], buffer_1_out[4], buffer_1_out[5], buffer_1_out[6], buffer_1_out[7]);
  not not_2 (zero, or_2_out);
endmodule

module sh_l (
  input  cin,
  input  [7:0] in_2,
  output [7:0] out_3,
  output cout
);


  assign cout = in_2[7];
  assign out_3 = {in_2[6:0], cin};
endmodule

module sh_r (
  input  [7:0] in_1,
  input  cin,
  output cout,
  output [7:0] out_4
);


  assign cout = in_1[0];
  assign out_4 = {cin, in_1[7:1]};
endmodule

module clock (
  output clk,
  output clk_e,
  output clk_s
);

  wire clock_1_out, decoder_1_out0, decoder_1_out2;
  wire [1:0] counter_1_q;

  Clock clock_1 (.out(clock_1_out));
  Counter #(.width(2), .max('h3)) counter_1 (.Q(counter_1_q), .clk(clock_1_out));  // open: load, D, count, carry, clr
  Decoder #(.select(2)) decoder_1 (
    .out0(decoder_1_out0), .out1(clk_s), .out2(decoder_1_out2), .sel(counter_1_q));  // open: out3, en
  or or_1 (clk, decoder_1_out0, clk_s);
  or or_2 (clk_e, decoder_1_out0, clk_s, decoder_1_out2);
endmodule
